# Fritzing sketch Taster with Interrupt (saved by Fritzing 0.9.2b)
breadboards: 1

parts:
  S1 = Pushbutton [package="[THT]"]
  R2 = Resistor [tolerance=±5% resistance=680 package="0805 [SMD]"]
  R4 = Resistor [tolerance=±0.1% resistance=1.1k package=THT]

nets:
  N1: S1.Pin_1, S1.Pin_2, S1.Pin_3, S1.Pin_4, R4.Pin_0
  N2: R2.Pin_0, R4.Pin_1

notes:
  Ground
  Port 9, Bus 2
  Gpio 23 (3v)
  intB Bus 2 (5v)
