# Fritzing sketch Use Pulldown on sensors (saved by Fritzing 0.9.2b)
breadboards: 1

parts:
  R1 = Photocell (LDR) [package=THT]
  R2 = Resistor [tolerance=±5% resistance=0.60k package=THT]

nets:
  N1: R1.pin_0, R2.Pin_0

notes:
  Pulldown mode
