# Fritzing sketch mcp3008 sketch (saved by Fritzing 0.9.2b)
breadboards: 1

parts:
  Raspberry_Pi1 = Raspberry Pi 2
  IC1 = IC, DIP package, 16 pins [chip_label=MCP3008]
  R2 = Resistor [tolerance=±5% resistance=10k package=THT]
  R3 = Resistor [tolerance=±5% resistance=10k package=THT]
  R4 = Resistor [tolerance=±0.05% resistance=10k package=THT]
  R5 = Photocell (LDR) [package=THT]
  R6 = Photocell (LDR) [package=THT]
  R7 = Photocell (LDR) [package=THT]

nets:
  N1: Raspberry_Pi1.3v3, IC1.pin15, IC1.pin16, R2.Pin_1, R3.Pin_1, R4.Pin_1
  N2: Raspberry_Pi1.GPIO25, IC1.pin10
  N3: Raspberry_Pi1.GPIO24, IC1.pin11
  N4: Raspberry_Pi1.GPIO23, IC1.pin12
  N5: Raspberry_Pi1.GPIO18, IC1.pin13
  N6: Raspberry_Pi1.GND, IC1.pin9, IC1.pin14, R5.pin_1, R6.pin_1, R7.pin_1
  N7: IC1.pin1, R3.Pin_0, R5.pin_0
  N8: IC1.pin2, R2.Pin_0, R6.pin_0
  N9: IC1.pin3, R4.Pin_0, R7.pin_0
