# Fritzing sketch mcp3008 spidev (saved by Fritzing 0.9.2b)
breadboards: 1

parts:
  IC1 = IC, DIP package, 16 pins [chip_label=MCP3008]
  R2 = Resistor [tolerance=±5% resistance=10k package=THT]
  R3 = Resistor [tolerance=±5% resistance=10k package=THT]
  R5 = Photocell (LDR) [package=THT]
  R6 = Photocell (LDR) [package=THT]
  R7 = Photocell (LDR) [package=THT]
  Pi1 = Adafruit Pi Cobbler  # not connected
  Pi2 = Adafruit Pi Cobbler  # not connected
  J2 = T Cobbler Plus
  R8 = Resistor [tolerance=±5% resistance=10k package=THT]
  R9 = Resistor [tolerance=±5% resistance=10k package=THT]

nets:
  N1: IC1.pin1, R3.Pin_0, R6.pin_0
  N2: IC1.pin2, R2.Pin_0, R5.pin_0
  N3: IC1.pin3, R7.pin_0, R9.Pin_0
  N4: IC1.pin4, R8.Pin_0
  N5: IC1.pin9, IC1.pin14, R5.pin_1, R6.pin_1, R7.pin_1, J2.GND#5
  N6: IC1.pin10, J2.CE0
  N7: IC1.pin11, J2.MOSI
  N8: IC1.pin12, J2.MISO
  N9: IC1.pin13, J2.SCLK
  N10: IC1.pin15, IC1.pin16, R2.Pin_1, R3.Pin_1, J2.3V3, R8.Pin_1, R9.Pin_1

custom parts:
  Adafruit Pi Cobbler: Adafruit Pi Cobbler GPIO Breakout for Raspberry Pi
  T Cobbler Plus: The T-Cobbler Plus is an add on prototyping board from Adafruit specifically designed for the Raspberry Pi B+ that can break out all those tasty power, GPIO, I2C and SPI pins from the 40-pin header onto a solderless breadboard. This set will make "cobbling together" prototypes with the Pi super easy. The T-Cobbler Plus can plug into any solderless breadboard.
